# Fritzing sketch hopeworks_codeday_fritzing_project (saved by Fritzing 0.9.3b)
circuit board: 6.64306cm x 4.4928cm
breadboards: 1

parts:
  VCC = Battery
  LED = smd LED [color="Red (633nm)" package="0805 [SMD]"]
  Photon_Photoresistor_Project = Photon
  Photoresistor = PHOTOCELL [package=photocell]
  R1_10kΩ = Resistor [tolerance=±5% resistance=10k package="0402 [SMD]"]
  R2_330Ω = Resistor [tolerance=±5% resistance=330 package="0402 [SMD]"]

nets:
  N1: VCC.-, Photon_Photoresistor_Project.GND, R1_10kΩ.Pin_1, R2_330Ω.Pin_1
  N2: VCC.+, Photon_Photoresistor_Project.3V3, Photoresistor.P$1
  N3: LED.cathode, R2_330Ω.Pin_0
  N4: LED.anode, Photon_Photoresistor_Project.D0
  N5: Photon_Photoresistor_Project.A0, Photoresistor.P$2, R1_10kΩ.Pin_0

notes:
  -
  +
